# Fritzing sketch button (saved by Fritzing 0.9.2b)
breadboards: 1

parts:
  Part1 = Arduino Uno (Rev3)
  LED1 = LED - 3mm [color="Red (633nm)" package="3 mm [THT]"]
  R1 = Resistor [tolerance=±5% resistance=220 part_number=1k package="2010 [SMD]"]
  S4 = Pushbutton [package="[SMD]"]

nets:
  N1: Part1.D13/SCK, S4.Pin_1, S4.Pin_2
  N2: Part1.GND, LED1.cathode
  N3: LED1.anode, R1.Pin_0
  N4: R1.Pin_1, S4.Pin_3, S4.Pin_4

notes:
  220 Ω
